# Fritzing sketch RaspberryServo (saved by Fritzing 0.9.3b)
breadboards: 1

parts:
  Raspberry_Pi_1 = Raspberry Pi 3 [part_number=RPI-3-V1.2]
  HC-SR04_Sensor_1 = HC-SR04 Ultrasonic Distance Sensor
  R1 = Resistor [tolerance=±5% resistance=470 package=THT]
  R2 = Resistor [tolerance=±5% resistance=330 package=THT]
  HC-SR04_Sensor_2 = HC-SR04 Ultrasonic Distance Sensor
  R3 = Resistor [tolerance=±5% resistance=470 package=THT]
  R4 = Resistor [tolerance=±5% resistance=330 package=THT]
  S1 = Momentary Switch [package=ksa_sealed_tac_switch]
  R5 = Resistor [tolerance=±5% resistance=1k package="0805 [SMD]"]
  R6 = Resistor [tolerance=±5% resistance=1k package="0805 [SMD]"]
  S2 = Momentary Switch [package=ksa_sealed_tac_switch]
  LED1 = RGB LED (com. cathode, rgb) [package="5 mm [THT]"]
  LED2 = RGB LED (com. cathode, rgb) [package="5 mm [THT]"]
  R7 = Resistor [tolerance=±5% resistance=1k package="0402 [SMD]"]
  INA1 = INA219 DC Current Sensor Breakout
  J1 = Basic Servo
  R8 = Resistor [tolerance=±5% resistance=470 package="0805 [SMD]"]
  R9 = Resistor [tolerance=±5% resistance=470 package="0805 [SMD]"]
  R10 = Resistor [tolerance=±5% resistance=1k package="0805 [SMD]"]

nets:
  N1: Raspberry_Pi_1.GPIO2, INA1.SDA
  N2: Raspberry_Pi_1.GPIO3, INA1.SCL
  N3: Raspberry_Pi_1.GPIO21, LED1.blue_anode, LED2.blue_anode
  N4: Raspberry_Pi_1.GPIO20, LED1.green_anode, LED2.green_anode
  N5: Raspberry_Pi_1.GPIO16, LED1.red_anode, LED2.red_anode
  N6: Raspberry_Pi_1.GPIO12, R7.Pin_1
  GND: Raspberry_Pi_1.GND, HC-SR04_Sensor_1.GND, R1.Pin_1, R3.Pin_1, R5.Pin_1, R6.Pin_1, INA1.GND, J1.gnd, R10.Pin_1
  N7: Raspberry_Pi_1.ID_SC, S1.1, R5.Pin_0
  N8: Raspberry_Pi_1.GPIO7, R6.Pin_0, S2.1
  N9: Raspberry_Pi_1.GPIO8, R3.Pin_0, R4.Pin_1
  N10: Raspberry_Pi_1.GPIO25, HC-SR04_Sensor_2.TRIG
  N11: Raspberry_Pi_1.GPIO24, R1.Pin_0, R2.Pin_1
  N12: Raspberry_Pi_1.GPIO23, HC-SR04_Sensor_1.TRIG
  VCC: Raspberry_Pi_1.5V, HC-SR04_Sensor_1.VCC, HC-SR04_Sensor_2.VCC, INA1.VCC, INA1.Vin+, R8.Pin_1, R9.Pin_1
  N13: HC-SR04_Sensor_1.ECHO, R2.Pin_0
  N14: HC-SR04_Sensor_2.ECHO, R4.Pin_0
  N15: S1.3, R9.Pin_0
  N16: S2.3, R8.Pin_0
  N17: LED1.common_cathode, LED2.common_cathode, R10.Pin_0
  N18: R7.Pin_0, J1.pulse
  N19: INA1.Vin-, J1.vcc

custom parts:
  INA219 DC Current Sensor Breakout: INA DC Current Sensor Breakout
